# Fritzing sketch Final-Globlock (saved by Fritzing 0.8.7b)
breadboards: 1

parts:
  U1 = ID-12_20 [package=id-12_smd]
  Part2 = Arduino Uno (Rev3)

nets:
  N1: U1.GNDT, U1.+_-, Part2.GND
  5V: U1.RES, U1.5V, Part2.5V
  N2: U1.D0, Part2.D9_PWM
