# Fritzing sketch Original-Globlock (saved by Fritzing 0.8.7b)
breadboards: 1

parts:
  U1 = ID-12_20 [package=id-12_smd]
  Part2 = Arduino Uno (Rev3)
  LCD1 = LCD screen
  R1 = Resistor [tolerance=±5% resistance=1k package=THT]
  R2 = Resistor [tolerance=±5% resistance=1k package=THT]
  J1 = Piezo Speaker  # not connected

nets:
  N1: U1.GNDT, U1.+_-, Part2.GND, LCD1.V0, LCD1.R/W, LCD1.LED-
  5V: U1.RES, U1.5V, Part2.5V, LCD1.VDD, R1.Pin_1, R2.Pin_0
  N2: U1.D0, Part2.D9_PWM
  N3: Part2.D8, LCD1.RS
  N4: Part2.D10_PWM/SS, LCD1.E
  N5: Part2.D4, LCD1.DB4
  N6: Part2.D5_PWM, LCD1.DB5
  N7: Part2.D6_PWM, LCD1.DB6
  N8: Part2.D7, LCD1.DB7
  N9: LCD1.LED+, R1.Pin_0
